# Fritzing sketch console8_zdi (saved by Fritzing 1.0.1rc)
breadboards: 1

parts:
  MH-ET_LIVE_ESP32_DEVKIT1 = MH-ET LIVE ESP32 DEVKIT 38 pins
  J2 = AVR ISP 6 Pin [package=2x3_lock]  # not connected
  J3 = female pin header, 1 pin [form="♀ (female)"]  # not connected
  J4 = female pin header, 1 pin [form="♀ (female)"]
  J5 = female pin header, 1 pin [form="♀ (female)"]
  J6 = female pin header, 1 pin [form="♀ (female)"]

nets:
  N1: MH-ET_LIVE_ESP32_DEVKIT1.IO26, J4.pin1
  N2: MH-ET_LIVE_ESP32_DEVKIT1.IO27, J5.pin1
  N3: MH-ET_LIVE_ESP32_DEVKIT1.GND#58, J6.pin1

notes:
  Console8 ZDI port
  ESP32 DEVKIT
  TDI - ESP IO27
  TCK - ESP IO26
  Lower left pin
  Lower middle pin
  Top left pin (GND)

custom parts:
  MH-ET LIVE ESP32 DEVKIT 38 pins: http://mh.nodebb.com/topic/2/mh-et-live-esp32-devkit
  AVR ISP 6 Pin: AVR ISP 6 Pin This is the reduced ISP connector for AVR programming. Common on Arduino. This footprint will take up less PCB space and can be used with a 10-pin to 6-pin adapter such as SKU: BOB-08508
